// Logisim project MyCPU.circ as structural Verilog: 2 circuits, main circuit MyCPU
// 2
module MyCPU (
  input  RESET,
  input  CLK_EN
);

  wire alu_1_zero, and_1_out, CLK_out, CLK_PULSE_out, CZ_out, not_1_out, or_1_out, or_2_out, or_3_out;
  wire [3:0] INS_REG_q, STP_CNTR_q;
  wire [6:0] bit_extender_2_out, pull_resistor_2_node;
  wire [7:0] alu_1_res, bit_extender_1_out, MEM_ADR_q, PRG_CNTR_q, pull_resistor_1_node, ram_1_data, REG_A_q,
       REG_B_q;
  wire [7:4] INS_REG_q_2;
  wire [23:0] rom_1_data;

  // Probe on pull_resistor_1_node
  // Probe on pull_resistor_1_node
  // Probe on pull_resistor_1_node
  Pull_Resistor pull_resistor_1 (.node(pull_resistor_1_node));
  Register INS_REG (
    .D(pull_resistor_1_node), .en(rom_1_data[23]), .Q({INS_REG_q_2, INS_REG_q}), .clk(or_2_out), .clr(RESET));
  not not_1 (not_1_out, or_2_out);
  assign pull_resistor_1_node = rom_1_data[22] ? bit_extender_1_out : 8'bz;  // Controlled_Buffer controlled_buffer_1
  // Probe on bit_extender_1_out
  assign bit_extender_1_out = {{4{1'b0}}, INS_REG_q};  // Bit_Extender bit_extender_1
  // Probe on INS_REG_q_2
  Counter #(.width(4), .max('h7)) STP_CNTR (
    .Q(STP_CNTR_q), .clk(not_1_out), .clr(or_1_out));  // open: load, D, count, carry
  or or_1 (or_1_out, RESET, rom_1_data[8]);
  or or_2 (or_2_out, CLK_PULSE_out, and_1_out);
  or or_3 (or_3_out, rom_1_data[20], CZ_out);
  and and_1 (and_1_out, CLK_EN, CLK_out);
  assign pull_resistor_1_node = rom_1_data[19] ? PRG_CNTR_q : 8'bz;  // Controlled_Buffer controlled_buffer_2
  Counter PRG_CNTR (
    .load(or_3_out), .D(pull_resistor_1_node), .count(rom_1_data[21]), .Q(PRG_CNTR_q), .clk(or_2_out),
    .clr(RESET));  // open: carry
  Button CLK_PULSE (.out(CLK_PULSE_out));
  Clock CLK (.out(CLK_out));
  Register MEM_ADR (.D(pull_resistor_1_node), .en(rom_1_data[18]), .Q(MEM_ADR_q), .clk(or_2_out), .clr(RESET));
  ROM #(.dataWidth(24)) rom_1 (.addr({INS_REG_q_2, STP_CNTR_q}), .data(rom_1_data));  // open: sel
  RAM #(.bus("separate")) ram_1 (
    .addr(MEM_ADR_q), .din(pull_resistor_1_node), .data(ram_1_data), .str(rom_1_data[17]), .clk(or_2_out));  // open: sel, ld, clr
  assign pull_resistor_1_node = rom_1_data[16] ? ram_1_data : 8'bz;  // Controlled_Buffer controlled_buffer_3
  // Probe on rom_1_data[8]
  assign pull_resistor_1_node = rom_1_data[14] ? REG_A_q : 8'bz;  // Controlled_Buffer controlled_buffer_4
  Register REG_A (.D(pull_resistor_1_node), .en(rom_1_data[15]), .Q(REG_A_q), .clk(or_2_out), .clr(RESET));
  // Probe on rom_1_data[23]
  // Probe on rom_1_data[21]
  // Probe on rom_1_data[22]
  assign pull_resistor_1_node = rom_1_data[12] ? REG_B_q : 8'bz;  // Controlled_Buffer controlled_buffer_5
  Register REG_B (.D(pull_resistor_1_node), .en(rom_1_data[13]), .Q(REG_B_q), .clk(or_2_out), .clr(RESET));
  ALU alu_1 (
    .B(REG_B_q), .SUM(rom_1_data[11]), .A(REG_A_q), .RES(alu_1_res), .ZERO(alu_1_zero));  // open: SUB, MUL, DIV, MOD, XOR, OR, AND, NOT
  // Probe on rom_1_data[19]
  // Probe on rom_1_data[18]
  // Probe on rom_1_data[20]
  and CZ (CZ_out, alu_1_zero, rom_1_data[7]);
  // Probe on rom_1_data[16]
  // Probe on rom_1_data[14]
  // Probe on rom_1_data[17]
  // Probe on rom_1_data[15]
  assign pull_resistor_1_node = rom_1_data[10] ? alu_1_res : 8'bz;  // Controlled_Buffer controlled_buffer_6
  assign pull_resistor_1_node = rom_1_data[11] ? alu_1_res : 8'bz;  // Controlled_Buffer controlled_buffer_7
  // Probe on rom_1_data[11]
  // Probe on rom_1_data[13]
  // Probe on rom_1_data[12]
  Bit_Extender #(.out_width(7)) bit_extender_2 (.in(pull_resistor_1_node), .out(bit_extender_2_out));
  Pull_Resistor pull_resistor_2 (.node(pull_resistor_2_node));
  assign pull_resistor_2_node = rom_1_data[9] ? bit_extender_2_out : 7'bz;  // Controlled_Buffer controlled_buffer_8
  // Probe on rom_1_data[9]
  // Probe on rom_1_data[10]
  TTY #(.trigger("falling")) tty_1 (.data(pull_resistor_2_node), .clk(or_2_out), .clr(RESET));  // open: we
  // Probe on rom_1_data[7]

  // Notes on the sheet:
  //   CLK
  //   CLR
  //   Instruction Decoder
  //   contents of rom_1 (hex, n*v repeats v):
  //   c0000 a10000 440000 18000 100 27*0 c0000 a10000 440000 12000 8800 1 26*0 c0000 a10000 440000 110000
  //   100 11*0 c0000 a10000 440000 10010 12*0 c0000 a10000 44000 10200 200 100
  //   Program Memory
  //   BUS
  //   CLK
  //   CLR
endmodule

module ALU (
  input  [7:0] A,
  input  [7:0] B,
  input  SUM,
  input  SUB,
  input  MUL,
  input  DIV,
  input  MOD,
  input  XOR,
  input  OR,
  input  AND,
  input  NOT,
  output ZERO,
  output [7:0] RES
);

  wire CARRY_OUT, nor_1_out, not_1_out;
  wire [7:0] adder_1_out, and_1_out, comparator_1_eq, controlled_buffer_1_out, divider_1_out, divider_1_rem,
       multiplier_1_out, or_1_out, subtractor_1_out, xor_1_out;
  wire [7:1] STATUS_q;

  Adder adder_1 (.a(A), .b(B), .out(adder_1_out), .cout(CARRY_OUT));  // open: cin
  // Probe on adder_1_out
  Subtractor subtractor_1 (.a(A), .b(B), .out(subtractor_1_out));  // open: bin, bout
  // Probe on subtractor_1_out
  Multiplier multiplier_1 (.a(A), .b(B), .out(multiplier_1_out));  // open: cin, cout
  // Probe on multiplier_1_out
  Divider divider_1 (.a(A), .b(B), .out(divider_1_out), .rem(divider_1_rem));  // open: upper
  // Probe on divider_1_out
  // Probe on divider_1_rem
  Pull_Resistor pull_resistor_1 (.node(SUM));
  assign controlled_buffer_1_out = SUM ? adder_1_out : 8'bz;  // Controlled_Buffer controlled_buffer_1
  assign controlled_buffer_1_out = SUB ? subtractor_1_out : 8'bz;  // Controlled_Buffer controlled_buffer_2
  Pull_Resistor pull_resistor_2 (.node(SUB));
  Pull_Resistor pull_resistor_3 (.node(MUL));
  assign controlled_buffer_1_out = MUL ? multiplier_1_out : 8'bz;  // Controlled_Buffer controlled_buffer_3
  assign controlled_buffer_1_out = DIV ? divider_1_out : 8'bz;  // Controlled_Buffer controlled_buffer_4
  Pull_Resistor pull_resistor_4 (.node(MOD));
  Pull_Resistor pull_resistor_5 (.node(DIV));
  assign controlled_buffer_1_out = XOR ? xor_1_out : 8'bz;  // Controlled_Buffer controlled_buffer_5
  assign controlled_buffer_1_out = MOD ? divider_1_rem : 8'bz;  // Controlled_Buffer controlled_buffer_6
  Pull_Resistor pull_resistor_6 (.node(XOR));
  Pull_Resistor pull_resistor_7 (.node(OR));
  Comparator comparator_1 (.a({8{1'b0}}), .b(controlled_buffer_1_out), .eq(comparator_1_eq[0]));  // open: gt, lt
  assign controlled_buffer_1_out = AND ? and_1_out : 8'bz;  // Controlled_Buffer controlled_buffer_7
  assign controlled_buffer_1_out = OR ? or_1_out : 8'bz;  // Controlled_Buffer controlled_buffer_8
  Pull_Resistor pull_resistor_8 (.node(AND));
  Pull_Resistor pull_resistor_9 (.node(NOT));
  assign and_1_out = A & B;  // AND_Gate and_1, 8 bits wide
  assign or_1_out = A | B;  // OR_Gate or_1, 8 bits wide
  assign xor_1_out = A ^ B;  // XOR_Gate xor_1, 8 bits wide
  assign RES = NOT ? ~controlled_buffer_1_out : 8'bz;  // Controlled_Inverter controlled_inverter_1
  assign RES = not_1_out ? controlled_buffer_1_out : 8'bz;  // Controlled_Buffer controlled_buffer_9
  not not_1 (not_1_out, NOT);
  nor nor_1 (nor_1_out, SUM, SUB, MUL, DIV, MOD, XOR, OR, AND, NOT);
  Pull_Resistor pull_resistor_10 (.node(comparator_1_eq));
  Pull_Resistor pull_resistor_11 (.node(RES));
  Register STATUS (.D(comparator_1_eq), .Q({STATUS_q, ZERO}), .clk(nor_1_out));  // open: en, clr
endmodule
