// Logisim project MyCPU_Pipelined.circ as structural Verilog: 4 circuits, main circuit MyCPU
// 2
module MyCPU (
  input  [4:0] Opcode,
  input  [1:0] DstReg,
  input  [1:0] SrcReg1,
  input  [1:0] SrcReg2,
  input  [4:0] Fn,
  input  PRG_MODE
);

  wire button_1_out, CLK, CLR, decoder_1_out0, decoder_1_out1, decoder_1_out2, decoder_1_out3,
       decoder_1_out4, decoder_1_out5, decoder_1_out6, decoder_1_out7, not_1_out, not_2_out, or_1_out;
  wire [3:0] bit_extender_1_out, counter_2_q;
  wire [7:0] alu_1_res, counter_1_q, multiplexer_1_out, ram_2_data, register_1_q, register_file_1_readdata1,
       register_file_1_readdata2;
  wire [15:0] controlled_buffer_1_out, ram_1_data, rom_2_data;
  wire [31:0] register_file_1_dbg;

  Counter counter_1 (.Q(counter_1_q));  // open: load, D, count, carry, clk, clr
  Counter #(.width(4), .max('hf)) counter_2 (.Q(counter_2_q), .clk(CLK), .clr(CLR));  // open: load, D, count, carry
  or or_1 (or_1_out, CLK, button_1_out);
  // Probe on ram_1_data
  RAM #(.dataWidth(16)) ram_1 (
    .addr(counter_1_q), .data(ram_1_data), .clk(or_1_out), .ld(not_2_out));  // open: sel, clr
  assign controlled_buffer_1_out = not_2_out ? ram_1_data : 16'bz;  // Controlled_Buffer controlled_buffer_1
  assign ram_1_data = not_1_out ? {Opcode, DstReg, SrcReg1, SrcReg2, Fn} : 16'bz;  // Controlled_Buffer controlled_buffer_2
  not not_1 (not_1_out, not_2_out);
  not not_2 (not_2_out, PRG_MODE);
  Button button_1 (.out(button_1_out));
  Pull_Resistor pull_resistor_1 (.node(controlled_buffer_1_out));
  Bit_Extender #(.in_width(5), .out_width(4)) bit_extender_1 (
    .in(controlled_buffer_1_out[15:11]), .out(bit_extender_1_out));
  Button button_2 (.out(CLR));
  Button button_3 (.out(CLK));
  ROM #(.dataWidth(16)) rom_1 ();  // open: addr, data, sel
  ROM #(.dataWidth(16)) rom_2 (.addr({bit_extender_1_out, counter_2_q}), .data(rom_2_data));  // open: sel
  Register_File register_file_1 (
    .WriteData(alu_1_res), .CLK(CLK), .WRS1(controlled_buffer_1_out[10:9]),
    .RRS1(controlled_buffer_1_out[8:7]), .RRS2(controlled_buffer_1_out[6:5]),
    .ReadData1(register_file_1_readdata1), .ReadData2(register_file_1_readdata2), .DBG(register_file_1_dbg),
    .RESET(CLR));
  // Probe on register_file_1_dbg
  Multiplexer #(.width(8), .enable("false")) multiplexer_1 (
    .in0(register_file_1_readdata2), .in1(ram_2_data), .out(multiplexer_1_out),
    .sel(controlled_buffer_1_out[4]));
  Bit_Extender #(.in_width(5), .out_width(3)) bit_extender_2 (.in(controlled_buffer_1_out[4:0]));  // open: out
  Register register_1 (.Q(register_1_q));  // open: D, en, clk, clr
  ALU alu_1 (
    .B(multiplexer_1_out), .SUM(decoder_1_out0), .SUB(decoder_1_out1), .MUL(decoder_1_out2),
    .DIV(decoder_1_out3), .MOD(decoder_1_out4), .A(register_file_1_readdata1), .XOR(decoder_1_out5),
    .OR(decoder_1_out6), .AND(decoder_1_out7), .RES(alu_1_res));  // open: NOT
  Pull_Resistor pull_resistor_2 (.node(rom_2_data[2:0]));
  Decoder #(.select(3), .enable("false")) decoder_1 (
    .out0(decoder_1_out0), .out1(decoder_1_out1), .out2(decoder_1_out2), .out3(decoder_1_out3),
    .out4(decoder_1_out4), .out5(decoder_1_out5), .out6(decoder_1_out6), .out7(decoder_1_out7),
    .sel(rom_2_data[2:0]));
  RAM ram_2 (.addr(register_1_q), .data(ram_2_data));  // open: sel, clk, ld, clr
  // Probe on multiplexer_1_out
  // Probe on register_file_1_readdata1
  // Probe on alu_1_res
  LED led_1 ();  // open: in

  // Notes on the sheet:
  //   contents of rom_1 (hex, n*v repeats v):
  //   c00 a100 4400 180 1 27*0 c00 a100 4400 120 88 1 26*0 c00 a100 4400 1100 1 27*0 c00 a100 440 102 2 1
  //   contents of rom_2 (hex, n*v repeats v):
  //   0 0 0 ff80 1 11*0 2 18*0 20 ff88 1 30*0 1 29*0 40 2 2 1
endmodule

module ALU (
  input  [7:0] A,
  input  [7:0] B,
  input  SUM,
  input  SUB,
  input  MUL,
  input  DIV,
  input  MOD,
  input  XOR,
  input  OR,
  input  AND,
  input  NOT,
  output [7:0] RES
);

  wire not_1_out;
  wire [7:0] adder_1_out, and_1_out, controlled_buffer_1_out, divider_1_out, divider_1_rem, multiplier_1_out,
       or_1_out, subtractor_1_out, xor_1_out;

  Pull_Resistor pull_resistor_1 (.node(B));
  Pull_Resistor pull_resistor_2 (.node(A));
  Adder adder_1 (.a(A), .b(B), .out(adder_1_out));  // open: cin, cout
  Subtractor subtractor_1 (.a(A), .b(B), .out(subtractor_1_out));  // open: bin, bout
  Multiplier multiplier_1 (.a(A), .b(B), .out(multiplier_1_out));  // open: cin, cout
  Divider divider_1 (.a(A), .b(B), .out(divider_1_out), .rem(divider_1_rem));  // open: upper
  assign controlled_buffer_1_out = SUM ? adder_1_out : 8'bz;  // Controlled_Buffer controlled_buffer_1
  // Probe on adder_1_out
  // Probe on subtractor_1_out
  // Probe on multiplier_1_out
  // Probe on divider_1_out
  // Probe on divider_1_rem
  Pull_Resistor pull_resistor_3 (.node(SUB));
  Pull_Resistor pull_resistor_4 (.node(SUM));
  assign controlled_buffer_1_out = SUB ? subtractor_1_out : 8'bz;  // Controlled_Buffer controlled_buffer_2
  assign controlled_buffer_1_out = MUL ? multiplier_1_out : 8'bz;  // Controlled_Buffer controlled_buffer_3
  Pull_Resistor pull_resistor_5 (.node(MUL));
  Pull_Resistor pull_resistor_6 (.node(DIV));
  assign controlled_buffer_1_out = XOR ? xor_1_out : 8'bz;  // Controlled_Buffer controlled_buffer_4
  assign controlled_buffer_1_out = DIV ? divider_1_out : 8'bz;  // Controlled_Buffer controlled_buffer_5
  assign controlled_buffer_1_out = MOD ? divider_1_rem : 8'bz;  // Controlled_Buffer controlled_buffer_6
  Pull_Resistor pull_resistor_7 (.node(XOR));
  Pull_Resistor pull_resistor_8 (.node(MOD));
  assign controlled_buffer_1_out = AND ? and_1_out : 8'bz;  // Controlled_Buffer controlled_buffer_7
  assign controlled_buffer_1_out = OR ? or_1_out : 8'bz;  // Controlled_Buffer controlled_buffer_8
  Pull_Resistor pull_resistor_9 (.node(AND));
  Pull_Resistor pull_resistor_10 (.node(OR));
  assign and_1_out = A & B;  // AND_Gate and_1, 8 bits wide
  assign or_1_out = A | B;  // OR_Gate or_1, 8 bits wide
  assign xor_1_out = A ^ B;  // XOR_Gate xor_1, 8 bits wide
  Pull_Resistor pull_resistor_11 (.node(NOT));
  assign RES = NOT ? ~controlled_buffer_1_out : 8'bz;  // Controlled_Inverter controlled_inverter_1
  Pull_Resistor pull_resistor_12 (.node(RES));
  assign RES = not_1_out ? controlled_buffer_1_out : 8'bz;  // Controlled_Buffer controlled_buffer_9
  not not_1 (not_1_out, NOT);
endmodule

module Register_File (
  input  RESET,
  input  [7:0] WriteData,
  input  CLK,
  input  [1:0] WRS1,
  input  [1:0] RRS1,
  input  [1:0] RRS2,
  output [31:0] DBG,
  output [7:0] ReadData1,
  output [7:0] ReadData2
);

  wire decoder_1_out0, decoder_1_out1, decoder_1_out2, decoder_1_out3;

  Pull_Resistor pull_resistor_1 (.node(RRS2));
  Pull_Resistor pull_resistor_2 (.node(WriteData));
  Pull_Resistor pull_resistor_3 (.node(CLK));
  Pull_Resistor pull_resistor_4 (.node(RRS1));
  Decoder #(.select(2), .enable("false")) decoder_1 (
    .out0(decoder_1_out0), .out1(decoder_1_out1), .out2(decoder_1_out2), .out3(decoder_1_out3), .sel(WRS1));
  Pull_Resistor pull_resistor_5 (.node(WRS1));
  Register register_1 (.D(WriteData), .en(decoder_1_out0), .Q(DBG[7:0]), .clk(CLK), .clr(RESET));
  Register register_2 (.D(WriteData), .en(decoder_1_out1), .Q(DBG[15:8]), .clk(CLK), .clr(RESET));
  Register register_3 (.D(WriteData), .en(decoder_1_out2), .Q(DBG[23:16]), .clk(CLK), .clr(RESET));
  Register register_4 (.D(WriteData), .en(decoder_1_out3), .Q(DBG[31:24]), .clk(CLK), .clr(RESET));
  Pull_Resistor pull_resistor_6 (.node(RESET));
  Multiplexer #(.select(2), .width(8), .enable("false")) multiplexer_1 (
    .in0(DBG[7:0]), .in1(DBG[15:8]), .in2(DBG[23:16]), .in3(DBG[31:24]), .out(ReadData1), .sel(RRS1));
  Multiplexer #(.select(2), .width(8), .enable("false")) multiplexer_2 (
    .in0(DBG[7:0]), .in1(DBG[15:8]), .in2(DBG[23:16]), .in3(DBG[31:24]), .out(ReadData2), .sel(RRS2));

  // Notes on the sheet:
  //   RRS1: pull=down
  //   RRS2: pull=down
  //   WriteData: pull=down
  //   CLK: pull=down
endmodule

module Module_Test (
  input  [7:0] in_1,
  input  [7:0] in_2,
  input  in_3,
  input  [9:0] in_4
);

  wire [7:0] alu_1_res, register_1_q, register_2_q;

  Register register_1 (.D(in_1), .Q(register_1_q), .clk(in_3));  // open: en, clr
  Register register_2 (.D(in_2), .Q(register_2_q), .clk(in_3));  // open: en, clr
  ALU alu_1 (
    .B(register_2_q), .SUM(in_4[9]), .SUB(in_4[8]), .MUL(in_4[7]), .DIV(in_4[6]), .MOD(in_4[5]),
    .A(register_1_q), .XOR(in_4[4]), .OR(in_4[3]), .AND(in_4[2]), .NOT(in_4[1]), .RES(alu_1_res));
  Pull_Resistor pull_resistor_1 (.node(alu_1_res));
  // Probe on alu_1_res
endmodule
